// Logisim project Ctl_Load_Store.circ as structural Verilog: 1 circuit, main circuit Load_Store
module Load_Store (
  input  [15:0] Instruction,
  input  Enable,
  input  Clk,
  input  Reset,
  input  [31:0] Stack_Pointer,
  output Store,
  output Load,
  output PC_Hold,
  output [2:0] Rmd,
  output [31:0] RAM_Addr
);

  wire inBascule, outBascule;
  wire [2:0] bit_extender_1_out;
  wire [31:0] bit_extender_2_out;

  assign bit_extender_1_out = {{2{Enable}}, Enable};  // Bit_Extender bit_extender_1
  assign bit_extender_2_out = {{31{Enable}}, Enable};  // Bit_Extender bit_extender_2
  buf and_1 (Store, Enable);  // AND_Gate
  buf and_2 (Load, Enable);  // AND_Gate
  buf and_3 (PC_Hold, Enable);  // AND_Gate
  assign Rmd = bit_extender_1_out;  // AND_Gate and_4, 3 bits wide AND_Gate
  assign RAM_Addr = bit_extender_2_out;  // AND_Gate and_5, 32 bits wide AND_Gate
  D_Flip_Flop d_ff_1 (.D(inBascule), .clk(Clk), .Q(outBascule));  // open: Qn, preset, reset

  // Other names for the same wires on the sheet: clock = Clk; enableOut = Enable

  // Notes on the sheet:
  //   Instruction: pull=down
  //   Delay load and hold PC for 1 cycle for the RAM to send out requested data 
endmodule
