// Logisim project Ctl_SP_Address.circ as structural Verilog: 1 circuit, main circuit SP_Address
module SP_Address (
  input  [31:0] Stack_Pointer,
  input  [15:0] Instruction,
  input  Enable,
  output [31:0] New_Stack_Pointer,
  output Write_Enable
);

  wire septBit;
  wire [6:0] bitselector_2_out;
  wire [31:0] adder_1_out, bit_extender_2_out, multiplexer_1_out, septDernBits, subtractor_1_out;

  BitSelector #(.width(16)) bitselector_1 (.in(Instruction), .out(septBit), .sel(4'b0111));
  BitSelector #(.group(7), .width(16)) bitselector_2 (.in(Instruction), .out(bitselector_2_out), .sel(2'b00));
  assign septDernBits = {{25{1'b0}}, bitselector_2_out};  // Bit_Extender bit_extender_1
  Adder #(.width(32)) adder_1 (.a(Stack_Pointer), .b(septDernBits), .out(adder_1_out));  // open: cin, cout
  Subtractor #(.width(32)) subtractor_1 (
    .a(Stack_Pointer), .b(septDernBits), .out(subtractor_1_out));  // open: bin, bout
  Multiplexer #(.enable("false"), .width(32)) multiplexer_1 (
    .in0(adder_1_out), .in1(subtractor_1_out), .out(multiplexer_1_out), .sel(septBit));
  assign New_Stack_Pointer = multiplexer_1_out & bit_extender_2_out;  // AND_Gate and_1, 32 bits wide
  assign bit_extender_2_out = {{31{Enable}}, Enable};  // Bit_Extender bit_extender_2

  assign Write_Enable = Enable;

  // Notes on the sheet:
  //   Pull output low on Enable = 0
endmodule
