// Logisim project Ctl_Shift_Add_Sub_Mov.circ as structural Verilog: 1 circuit, main circuit Shift_Add_Sub_Mov
module Shift_Add_Sub_Mov (
  input  Enable,
  input  [15:0] Instruction,
  output [3:0] Flags_Update_Mask,
  output Carry,
  output Imm32_Enable,
  output [2:0] Rm,
  output [2:0] Rn,
  output [2:0] Rd,
  output [4:0] Imm5,
  output [31:0] Imm32,
  output [3:0] ALU_Opcode
);

  wire Add_imm8, Add_Immediate, Add_OR_Sub_Register, Add_Register, and_38_out, and_39_out, and_40_out,
       and_41_out, and_42_out, and_43_out, and_45_out, and_46_out, and_47_out, and_48_out, and_49_out,
       and_50_out, and_51_out, and_52_out, and_53_out, and_57_out, and_58_out, and_59_out, and_60_out,
       and_61_out, and_62_out, and_64_out, Arithmetic_Shift_Right_bool, bit_sortant_decallage_left_logic,
       bit_sortant_decallage_right_logic, Cmp_Immediate, comparator_17_eq, comparator_18_eq,
       comparator_19_eq, comparator_20_eq, comparator_21_eq, comparator_22_eq, Imm8_Codop,
       Logical_Shift_Left_bool, Logical_Shift_Right_bool, Mov_Immediate, or_7_out, or_8_out,
       Out_Shift_C_Flag, Shift_Codop, Sub_imm8, Sub_Immediate, Sub_Register;
  wire [1:0] bit_extender_7_out, bit_extender_8_out, bit_extender_9_out, bit_extender_10_out,
       bit_extender_11_out, bit_extender_12_out, bit_extender_13_out, bit_extender_14_out,
       bit_extender_15_out, bit_extender_16_out, bit_extender_17_out, bit_extender_18_out,
       bit_extender_19_out, bit_extender_20_out;
  wire [2:0] Add_Immediate_output, Add_Register_output, adder_1_out, adder_2_out, and_1_out, and_2_out,
       and_3_out, and_4_out, and_9_out, and_10_out, and_11_out, and_12_out, and_13_out, and_14_out,
       and_15_out, and_16_out, and_17_out, and_18_out, and_19_out, and_20_out, and_21_out, and_22_out,
       bit_extender_5_out, bit_extender_6_out, bit_extender_27_out, bit_extender_29_out, bit_extender_30_out,
       bit_extender_31_out, bit_extender_32_out, bit_extender_36_out, bit_extender_37_out,
       bit_extender_38_out, bit_extender_39_out, bit_extender_40_out, bit_extender_41_out,
       bit_extender_42_out, bit_extender_43_out, bit_extender_44_out, bit_extender_45_out,
       bit_extender_46_out, bit_extender_47_out, bit_extender_48_out, bit_extender_49_out,
       bit_extender_50_out, bit_extender_51_out, bit_extender_52_out, bit_extender_57_out,
       bit_extender_58_out, bit_extender_59_out, bit_extender_60_out, bit_extender_61_out,
       bit_extender_62_out, bit_extender_67_out, bit_extender_68_out, bitselector_13_out, bitselector_14_out,
       bitselector_15_out, bitselector_16_out, Get_Rd, left_logical_shift_output, not_1_out,
       Out_Add_Subb_for_RD, Out_Shift_for_RD, output_for_RD_Flag, right_arithmetic_shift_output,
       right_logical_shift_output, Rm_For_Add_Value, Rm_Value, Rn_Value, Sub_Immediate_output,
       Sub_Register_output, subtractor_3_out, subtractor_4_out;
  wire [3:0] and_54_out, and_55_out, and_56_out, bit_extender_69_out, bit_extender_70_out,
       bit_extender_71_out, bitselector_6_out;
  wire [4:0] bit_extender_1_out, bit_extender_2_out, bit_extender_74_out, imm5_Value, subtractor_1_out,
       subtractor_2_out;
  wire [5:0] bitselector_4_out;
  wire [7:0] Add_imm8_output, adder_3_out, and_5_out, and_6_out, and_7_out, and_8_out, and_23_out,
       and_24_out, and_26_out, and_27_out, and_63_out, bit_extender_22_out, bit_extender_23_out,
       bit_extender_24_out, bit_extender_28_out, bit_extender_33_out, bit_extender_34_out,
       bit_extender_35_out, bit_extender_53_out, bit_extender_54_out, bit_extender_55_out,
       bit_extender_56_out, bit_extender_63_out, bit_extender_64_out, bit_extender_65_out,
       bit_extender_66_out, bit_extender_72_out, Cmp_Immediate_output, Imm8_Mov, Mov_Immediate_output,
       Out_Mov_CMP_For_RD, Sub_imm8_output, subtractor_5_out, subtractor_6_out;
  wire [10:0] bitselector_9_out, bitselector_10_out, bitselector_11_out, bitselector_12_out,
       bitselector_17_out, bitselector_18_out, bitselector_19_out, bitselector_20_out;
  wire [12:0] bitselector_7_out, bitselector_8_out;
  wire [31:0] bit_extender_21_out, bit_extender_25_out, bit_extender_26_out, shifter_1_out, shifter_2_out,
       shifter_3_out;

  assign bit_extender_1_out = {{2{1'b0}}, 3'b011};  // Bit_Extender bit_extender_1
  assign bit_extender_2_out = {{2{1'b0}}, 3'b001};  // Bit_Extender bit_extender_2
  BitSelector #(.group(3), .width(16)) bitselector_1 (.in(Instruction), .out(Rn_Value), .sel(3'b001));
  BitSelector #(.group(3), .width(16)) bitselector_2 (.in(Instruction), .out(Rm_For_Add_Value), .sel(3'b010));
  BitSelector #(.group(3), .width(16)) bitselector_3 (.in(Instruction), .out(Rm_Value), .sel(3'b001));
  BitSelector #(.group(6), .width(16)) bitselector_4 (.in(Instruction), .out(bitselector_4_out), .sel(2'b01));
  BitSelector #(.group(8), .width(16)) bitselector_5 (.in(Instruction), .out(Imm8_Mov), .sel(1'b0));
  BitSelector #(.group(4), .width(16)) bitselector_6 (.in(Instruction), .out(bitselector_6_out), .sel(2'b10));
  BitSelector #(.group(13), .width(16)) bitselector_7 (.in(Instruction), .out(bitselector_7_out), .sel(1'b1));
  BitSelector #(.group(13), .width(16)) bitselector_8 (.in(Instruction), .out(bitselector_8_out), .sel(1'b1));
  BitSelector #(.group(11), .width(16)) bitselector_9 (.in(Instruction), .out(bitselector_9_out), .sel(1'b1));
  BitSelector #(.group(11), .width(16)) bitselector_10 (.in(Instruction), .out(bitselector_10_out), .sel(1'b1));
  BitSelector #(.group(11), .width(16)) bitselector_11 (.in(Instruction), .out(bitselector_11_out), .sel(1'b1));
  BitSelector #(.group(11), .width(16)) bitselector_12 (.in(Instruction), .out(bitselector_12_out), .sel(1'b1));
  Subtractor #(.width(5)) subtractor_1 (
    .a(bit_extender_1_out), .b(imm5_Value), .out(subtractor_1_out));  // open: bin, bout
  Subtractor #(.width(5)) subtractor_2 (
    .a(imm5_Value), .b(bit_extender_2_out), .out(subtractor_2_out));  // open: bin, bout
  Bit_Extender #(.in_width(6), .out_width(5)) bit_extender_3 (.in(bitselector_4_out), .out(imm5_Value));
  Bit_Extender #(.in_width(4), .out_width(3)) bit_extender_4 (.in(bitselector_6_out), .out(Get_Rd));
  Bit_Extender #(.in_width(13), .out_width(3)) bit_extender_5 (.in(bitselector_7_out), .out(bit_extender_5_out));
  Bit_Extender #(.in_width(13), .out_width(3)) bit_extender_6 (.in(bitselector_8_out), .out(bit_extender_6_out));
  Bit_Extender #(.in_width(11), .out_width(2)) bit_extender_7 (.in(bitselector_9_out), .out(bit_extender_7_out));
  Bit_Extender #(.in_width(11), .out_width(2)) bit_extender_8 (.in(bitselector_10_out), .out(bit_extender_8_out));
  Bit_Extender #(.in_width(11), .out_width(2)) bit_extender_9 (.in(bitselector_11_out), .out(bit_extender_9_out));
  Bit_Extender #(.in_width(11), .out_width(2)) bit_extender_10 (.in(bitselector_12_out), .out(bit_extender_10_out));
  BitSelector #(.group(3), .width(16)) bitselector_13 (.in(Instruction), .out(bitselector_13_out), .sel(3'b011));
  BitSelector #(.group(3), .width(16)) bitselector_14 (.in(Instruction), .out(bitselector_14_out), .sel(3'b011));
  BitSelector #(.group(3), .width(16)) bitselector_15 (.in(Instruction), .out(bitselector_15_out), .sel(3'b011));
  BitSelector #(.group(3), .width(16)) bitselector_16 (.in(Instruction), .out(bitselector_16_out), .sel(3'b011));
  BitSelector #(.group(11), .width(16)) bitselector_17 (.in(Instruction), .out(bitselector_17_out), .sel(1'b1));
  BitSelector #(.group(11), .width(16)) bitselector_18 (.in(Instruction), .out(bitselector_18_out), .sel(1'b1));
  BitSelector #(.group(11), .width(16)) bitselector_19 (.in(Instruction), .out(bitselector_19_out), .sel(1'b1));
  BitSelector #(.group(11), .width(16)) bitselector_20 (.in(Instruction), .out(bitselector_20_out), .sel(1'b1));
  Bit_Extender #(.in_width(5), .out_width(2)) bit_extender_11 (.in(subtractor_1_out), .out(bit_extender_11_out));
  Bit_Extender #(.in_width(5), .out_width(2)) bit_extender_12 (.in(subtractor_2_out), .out(bit_extender_12_out));
  Bit_Extender #(.in_width(3), .out_width(2)) bit_extender_13 (.in(bitselector_13_out), .out(bit_extender_13_out));
  Bit_Extender #(.in_width(3), .out_width(2)) bit_extender_14 (.in(bitselector_14_out), .out(bit_extender_14_out));
  Bit_Extender #(.in_width(3), .out_width(2)) bit_extender_15 (.in(bitselector_15_out), .out(bit_extender_15_out));
  Bit_Extender #(.in_width(3), .out_width(2)) bit_extender_16 (.in(bitselector_16_out), .out(bit_extender_16_out));
  Bit_Extender #(.in_width(11), .out_width(2)) bit_extender_17 (.in(bitselector_17_out), .out(bit_extender_17_out));
  Bit_Extender #(.in_width(11), .out_width(2)) bit_extender_18 (.in(bitselector_18_out), .out(bit_extender_18_out));
  Bit_Extender #(.in_width(11), .out_width(2)) bit_extender_19 (.in(bitselector_19_out), .out(bit_extender_19_out));
  Bit_Extender #(.in_width(11), .out_width(2)) bit_extender_20 (.in(bitselector_20_out), .out(bit_extender_20_out));
  BitSelector #(.width(3)) bitselector_21 (
    .in(Rm_Value), .out(bit_sortant_decallage_left_logic), .sel(bit_extender_11_out));
  BitSelector #(.width(3)) bitselector_22 (
    .in(Rm_Value), .out(bit_sortant_decallage_right_logic), .sel(bit_extender_12_out));
  Comparator #(.width(3)) comparator_1 (.a(bit_extender_5_out), .b(3'b001), .eq(Imm8_Codop));  // open: gt, lt
  Comparator #(.width(3)) comparator_2 (.a(bit_extender_6_out), .b(3'b000), .eq(Shift_Codop));  // open: gt, lt
  Comparator #(.width(2)) comparator_3 (
    .a(bit_extender_7_out), .b(2'b00), .eq(Logical_Shift_Left_bool));  // open: gt, lt
  Comparator #(.width(2)) comparator_4 (
    .a(bit_extender_8_out), .b(2'b01), .eq(Logical_Shift_Right_bool));  // open: gt, lt
  Comparator #(.width(2)) comparator_5 (
    .a(bit_extender_9_out), .b(2'b10), .eq(Arithmetic_Shift_Right_bool));  // open: gt, lt
  Comparator #(.width(2)) comparator_6 (.a(bit_extender_10_out), .b(2'b11), .eq(Add_OR_Sub_Register));  // open: gt, lt
  Comparator #(.width(2)) comparator_7 (.a(bit_extender_13_out), .b(2'b00), .eq(Add_Register));  // open: gt, lt
  Comparator #(.width(2)) comparator_8 (.a(bit_extender_14_out), .b(2'b01), .eq(Sub_Register));  // open: gt, lt
  Comparator #(.width(2)) comparator_9 (.a(bit_extender_15_out), .b(2'b10), .eq(Add_Immediate));  // open: gt, lt
  Comparator #(.width(2)) comparator_10 (.a(bit_extender_16_out), .b(2'b11), .eq(Sub_Immediate));  // open: gt, lt
  Comparator #(.width(2)) comparator_11 (.a(bit_extender_17_out), .b(2'b00), .eq(Mov_Immediate));  // open: gt, lt
  Comparator #(.width(2)) comparator_12 (.a(bit_extender_18_out), .b(2'b01), .eq(Cmp_Immediate));  // open: gt, lt
  Comparator #(.width(2)) comparator_13 (.a(bit_extender_19_out), .b(2'b10), .eq(Add_imm8));  // open: gt, lt
  Comparator #(.width(2)) comparator_14 (.a(bit_extender_20_out), .b(2'b11), .eq(Sub_imm8));  // open: gt, lt
  assign bit_extender_21_out = {{29{Rm_Value[2]}}, Rm_Value};  // Bit_Extender bit_extender_21
  Adder #(.width(3)) adder_1 (.a(Rn_Value), .b(Rm_For_Add_Value), .out(adder_1_out));  // open: cin, cout
  assign bit_extender_22_out = {{5{Get_Rd[2]}}, Get_Rd};  // Bit_Extender bit_extender_22
  assign bit_extender_23_out = {{5{Get_Rd[2]}}, Get_Rd};  // Bit_Extender bit_extender_23
  assign bit_extender_24_out = {{5{Get_Rd[2]}}, Get_Rd};  // Bit_Extender bit_extender_24
  assign bit_extender_25_out = {{29{Rm_Value[2]}}, Rm_Value};  // Bit_Extender bit_extender_25
  assign bit_extender_26_out = {{29{Rm_Value[2]}}, Rm_Value};  // Bit_Extender bit_extender_26
  assign bit_extender_27_out = {{2{Add_OR_Sub_Register}}, Add_OR_Sub_Register};  // Bit_Extender bit_extender_27
  Subtractor #(.width(3)) subtractor_3 (.a(Rn_Value), .b(Rm_For_Add_Value), .out(subtractor_3_out));  // open: bin, bout
  Adder #(.width(3)) adder_2 (.a(Rn_Value), .b(Rm_For_Add_Value), .out(adder_2_out));  // open: cin, cout
  Subtractor #(.width(3)) subtractor_4 (.a(Rn_Value), .b(Rm_For_Add_Value), .out(subtractor_4_out));  // open: bin, bout
  assign bit_extender_28_out = {{7{Mov_Immediate}}, Mov_Immediate};  // Bit_Extender bit_extender_28
  Subtractor subtractor_5 (.a(bit_extender_22_out), .b(Imm8_Mov), .out(subtractor_5_out));  // open: bin, bout
  Adder adder_3 (.a(bit_extender_23_out), .b(Imm8_Mov), .out(adder_3_out));  // open: cin, cout
  Subtractor subtractor_6 (.a(bit_extender_24_out), .b(Imm8_Mov), .out(subtractor_6_out));  // open: bin, bout
  Bit_Extender #(.in_width(32), .out_width(3)) bit_extender_29 (.in(shifter_1_out), .out(bit_extender_29_out));
  Shifter #(.width(32)) shifter_1 (.in(bit_extender_21_out), .\dist (imm5_Value), .out(shifter_1_out));
  assign and_1_out = bit_extender_27_out & adder_1_out;  // AND_Gate and_1, 3 bits wide
  assign bit_extender_30_out = {{2{Add_OR_Sub_Register}}, Add_OR_Sub_Register};  // Bit_Extender bit_extender_30
  assign and_2_out = bit_extender_30_out & subtractor_3_out;  // AND_Gate and_2, 3 bits wide
  assign bit_extender_31_out = {{2{Add_OR_Sub_Register}}, Add_OR_Sub_Register};  // Bit_Extender bit_extender_31
  assign and_3_out = bit_extender_31_out & adder_2_out;  // AND_Gate and_3, 3 bits wide
  assign bit_extender_32_out = {{2{Add_OR_Sub_Register}}, Add_OR_Sub_Register};  // Bit_Extender bit_extender_32
  assign and_4_out = bit_extender_32_out & subtractor_4_out;  // AND_Gate and_4, 3 bits wide
  assign and_5_out = bit_extender_28_out & Imm8_Mov;  // AND_Gate and_5, 8 bits wide
  assign bit_extender_33_out = {{7{Cmp_Immediate}}, Cmp_Immediate};  // Bit_Extender bit_extender_33
  assign and_6_out = bit_extender_33_out & subtractor_5_out;  // AND_Gate and_6, 8 bits wide
  assign bit_extender_34_out = {{7{Add_imm8}}, Add_imm8};  // Bit_Extender bit_extender_34
  assign bit_extender_35_out = {{7{Sub_imm8}}, Sub_imm8};  // Bit_Extender bit_extender_35
  assign bit_extender_36_out = {{2{Logical_Shift_Left_bool}}, Logical_Shift_Left_bool};  // Bit_Extender bit_extender_36
  Bit_Extender #(.in_width(32), .out_width(3)) bit_extender_37 (.in(shifter_2_out), .out(bit_extender_37_out));
  Shifter #(.shift("lr"), .width(32)) shifter_2 (.in(bit_extender_25_out), .\dist (imm5_Value), .out(shifter_2_out));
  Bit_Extender #(.in_width(32), .out_width(3)) bit_extender_38 (.in(shifter_3_out), .out(bit_extender_38_out));
  Shifter #(.shift("ar"), .width(32)) shifter_3 (.in(bit_extender_26_out), .\dist (imm5_Value), .out(shifter_3_out));
  assign and_7_out = bit_extender_34_out & adder_3_out;  // AND_Gate and_7, 8 bits wide
  assign and_8_out = bit_extender_35_out & subtractor_6_out;  // AND_Gate and_8, 8 bits wide
  assign and_9_out = bit_extender_36_out & bit_extender_29_out;  // AND_Gate and_9, 3 bits wide
  assign bit_extender_39_out = {{2{Logical_Shift_Right_bool}}, Logical_Shift_Right_bool};  // Bit_Extender bit_extender_39
  assign bit_extender_40_out = {{2{Arithmetic_Shift_Right_bool}}, Arithmetic_Shift_Right_bool};  // Bit_Extender bit_extender_40
  assign bit_extender_41_out = {{2{Add_Register}}, Add_Register};  // Bit_Extender bit_extender_41
  assign and_10_out = bit_extender_41_out & and_1_out;  // AND_Gate and_10, 3 bits wide
  assign bit_extender_42_out = {{2{Sub_Register}}, Sub_Register};  // Bit_Extender bit_extender_42
  assign bit_extender_43_out = {{2{Add_Immediate}}, Add_Immediate};  // Bit_Extender bit_extender_43
  assign bit_extender_44_out = {{2{Sub_Immediate}}, Sub_Immediate};  // Bit_Extender bit_extender_44
  assign bit_extender_45_out = {{2{Shift_Codop}}, Shift_Codop};  // Bit_Extender bit_extender_45
  assign and_11_out = bit_extender_45_out & and_9_out;  // AND_Gate and_11, 3 bits wide
  assign bit_extender_46_out = {{2{Shift_Codop}}, Shift_Codop};  // Bit_Extender bit_extender_46
  assign and_12_out = bit_extender_39_out & bit_extender_37_out;  // AND_Gate and_12, 3 bits wide
  assign bit_extender_47_out = {{2{Shift_Codop}}, Shift_Codop};  // Bit_Extender bit_extender_47
  assign and_13_out = bit_extender_40_out & bit_extender_38_out;  // AND_Gate and_13, 3 bits wide
  assign bit_extender_48_out = {{2{Shift_Codop}}, Shift_Codop};  // Bit_Extender bit_extender_48
  assign and_14_out = bit_extender_42_out & and_2_out;  // AND_Gate and_14, 3 bits wide
  assign and_15_out = bit_extender_43_out & and_3_out;  // AND_Gate and_15, 3 bits wide
  assign and_16_out = bit_extender_44_out & and_4_out;  // AND_Gate and_16, 3 bits wide
  assign bit_extender_49_out = {{2{Enable}}, Enable};  // Bit_Extender bit_extender_49
  assign and_17_out = bit_extender_46_out & and_12_out;  // AND_Gate and_17, 3 bits wide
  assign and_18_out = bit_extender_47_out & and_13_out;  // AND_Gate and_18, 3 bits wide
  assign and_19_out = bit_extender_48_out & and_10_out;  // AND_Gate and_19, 3 bits wide
  assign bit_extender_50_out = {{2{Shift_Codop}}, Shift_Codop};  // Bit_Extender bit_extender_50
  assign and_20_out = bit_extender_50_out & and_14_out;  // AND_Gate and_20, 3 bits wide
  assign bit_extender_51_out = {{2{Shift_Codop}}, Shift_Codop};  // Bit_Extender bit_extender_51
  assign and_21_out = bit_extender_51_out & and_15_out;  // AND_Gate and_21, 3 bits wide
  assign bit_extender_52_out = {{2{Shift_Codop}}, Shift_Codop};  // Bit_Extender bit_extender_52
  assign and_22_out = bit_extender_52_out & and_16_out;  // AND_Gate and_22, 3 bits wide
  assign bit_extender_53_out = {{7{Imm8_Codop}}, Imm8_Codop};  // Bit_Extender bit_extender_53
  assign and_23_out = bit_extender_53_out & and_5_out;  // AND_Gate and_23, 8 bits wide
  assign bit_extender_54_out = {{7{Imm8_Codop}}, Imm8_Codop};  // Bit_Extender bit_extender_54
  assign and_24_out = bit_extender_54_out & and_6_out;  // AND_Gate and_24, 8 bits wide
  assign bit_extender_55_out = {{7{Imm8_Codop}}, Imm8_Codop};  // Bit_Extender bit_extender_55
  assign bit_extender_56_out = {{7{Imm8_Codop}}, Imm8_Codop};  // Bit_Extender bit_extender_56
  assign left_logical_shift_output = bit_extender_49_out & and_11_out;  // AND_Gate and_25, 3 bits wide
  assign bit_extender_57_out = {{2{Enable}}, Enable};  // Bit_Extender bit_extender_57
  assign bit_extender_58_out = {{2{Enable}}, Enable};  // Bit_Extender bit_extender_58
  assign bit_extender_59_out = {{2{Enable}}, Enable};  // Bit_Extender bit_extender_59
  assign and_26_out = bit_extender_55_out & and_7_out;  // AND_Gate and_26, 8 bits wide
  assign and_27_out = bit_extender_56_out & and_8_out;  // AND_Gate and_27, 8 bits wide
  assign right_logical_shift_output = bit_extender_57_out & and_17_out;  // AND_Gate and_28, 3 bits wide
  assign right_arithmetic_shift_output = bit_extender_58_out & and_18_out;  // AND_Gate and_29, 3 bits wide
  assign Add_Register_output = bit_extender_59_out & and_19_out;  // AND_Gate and_30, 3 bits wide
  assign bit_extender_60_out = {{2{Enable}}, Enable};  // Bit_Extender bit_extender_60
  assign Sub_Register_output = bit_extender_60_out & and_20_out;  // AND_Gate and_31, 3 bits wide
  assign bit_extender_61_out = {{2{Enable}}, Enable};  // Bit_Extender bit_extender_61
  assign Add_Immediate_output = bit_extender_61_out & and_21_out;  // AND_Gate and_32, 3 bits wide
  assign bit_extender_62_out = {{2{Enable}}, Enable};  // Bit_Extender bit_extender_62
  assign Sub_Immediate_output = bit_extender_62_out & and_22_out;  // AND_Gate and_33, 3 bits wide
  assign bit_extender_63_out = {{7{Enable}}, Enable};  // Bit_Extender bit_extender_63
  assign Mov_Immediate_output = bit_extender_63_out & and_23_out;  // AND_Gate and_34, 8 bits wide
  assign bit_extender_64_out = {{7{Enable}}, Enable};  // Bit_Extender bit_extender_64
  assign bit_extender_65_out = {{7{Enable}}, Enable};  // Bit_Extender bit_extender_65
  assign bit_extender_66_out = {{7{Enable}}, Enable};  // Bit_Extender bit_extender_66
  assign Cmp_Immediate_output = bit_extender_64_out & and_24_out;  // AND_Gate and_35, 8 bits wide
  assign Add_imm8_output = bit_extender_65_out & and_26_out;  // AND_Gate and_36, 8 bits wide
  assign Sub_imm8_output = bit_extender_66_out & and_27_out;  // AND_Gate and_37, 8 bits wide
  Comparator #(.width(3)) comparator_15 (
    .a(output_for_RD_Flag), .b(3'b000), .lt(Flags_Update_Mask[3]));  // open: gt, eq
  Comparator #(.width(3)) comparator_16 (
    .a(output_for_RD_Flag), .b(3'b000), .eq(Flags_Update_Mask[2]));  // open: gt, lt
  or or_1 (Flags_Update_Mask[1], Out_Shift_C_Flag, Out_Shift_C_Flag);
  and and_38 (and_38_out, Logical_Shift_Left_bool, 1'b1);
  and and_39 (and_39_out, Logical_Shift_Right_bool, 1'b1);
  and and_40 (and_40_out, Arithmetic_Shift_Right_bool, 1'b1);
  and and_41 (and_41_out, and_38_out, bit_sortant_decallage_left_logic);
  and and_42 (and_42_out, and_39_out, bit_sortant_decallage_right_logic);
  and and_43 (and_43_out, and_40_out, bit_sortant_decallage_right_logic);
  or or_2 (Out_Shift_C_Flag, and_41_out, and_42_out, and_43_out);
  Bit_Extender #(.out_width(3)) bit_extender_67 (.in(Out_Mov_CMP_For_RD), .out(bit_extender_67_out));
  assign output_for_RD_Flag = Out_Shift_for_RD | bit_extender_67_out | Out_Add_Subb_for_RD;  // OR_Gate or_3, 3 bits wide
  assign Out_Add_Subb_for_RD = Add_Immediate_output | Add_Register_output | Sub_Register_output | Sub_Immediate_output;  // OR_Gate or_4, 3 bits wide
  assign Out_Mov_CMP_For_RD = Add_imm8_output | Mov_Immediate_output | Cmp_Immediate_output | Sub_imm8_output;  // OR_Gate or_5, 8 bits wide
  assign Out_Shift_for_RD = left_logical_shift_output | right_logical_shift_output | right_arithmetic_shift_output;  // OR_Gate or_6, 3 bits wide
  assign bit_extender_68_out = {{2{Cmp_Immediate}}, Cmp_Immediate};  // Bit_Extender bit_extender_68
  assign not_1_out = ~bit_extender_68_out;  // NOT_Gate not_1, 3 bits wide
  assign Rd = not_1_out & output_for_RD_Flag;  // AND_Gate and_44, 3 bits wide
  and and_45 (and_45_out, Logical_Shift_Left_bool, Shift_Codop);
  and and_46 (and_46_out, Logical_Shift_Right_bool, Shift_Codop);
  and and_47 (and_47_out, Arithmetic_Shift_Right_bool, Shift_Codop);
  and and_48 (and_48_out, Add_Register, Shift_Codop);
  and and_49 (and_49_out, Sub_Register, Shift_Codop);
  and and_50 (and_50_out, Add_Immediate, Shift_Codop);
  and and_51 (and_51_out, Sub_Immediate, Shift_Codop);
  and and_52 (and_52_out, Add_imm8, Imm8_Codop);
  and and_53 (and_53_out, Sub_imm8, Imm8_Codop);
  or or_7 (or_7_out, Logical_Shift_Left_bool, Logical_Shift_Right_bool, Arithmetic_Shift_Right_bool);
  assign bit_extender_69_out = {{3{and_45_out}}, and_45_out};  // Bit_Extender bit_extender_69
  assign bit_extender_70_out = {{3{and_46_out}}, and_46_out};  // Bit_Extender bit_extender_70
  assign bit_extender_71_out = {{3{and_47_out}}, and_47_out};  // Bit_Extender bit_extender_71
  Comparator #(.width(1)) comparator_17 (.a(and_48_out), .b(1'b1), .eq(comparator_17_eq));  // open: gt, lt
  Comparator #(.width(1)) comparator_18 (.a(and_49_out), .b(1'b1), .eq(comparator_18_eq));  // open: gt, lt
  Comparator #(.width(1)) comparator_19 (.a(and_50_out), .b(1'b1), .eq(comparator_19_eq));  // open: gt, lt
  Comparator #(.width(1)) comparator_20 (.a(and_51_out), .b(1'b1), .eq(comparator_20_eq));  // open: gt, lt
  Comparator #(.width(1)) comparator_21 (.a(and_52_out), .b(1'b1), .eq(comparator_21_eq));  // open: gt, lt
  Comparator #(.width(1)) comparator_22 (.a(and_53_out), .b(1'b1), .eq(comparator_22_eq));  // open: gt, lt
  or or_8 (or_8_out, Mov_Immediate, Cmp_Immediate, Add_imm8, Sub_imm8);
  assign bit_extender_72_out = {{7{Imm32_Enable}}, Imm32_Enable};  // Bit_Extender bit_extender_72
  assign and_54_out = bit_extender_69_out & 4'b0010;  // AND_Gate and_54, 4 bits wide
  assign and_55_out = bit_extender_70_out & 4'b0011;  // AND_Gate and_55, 4 bits wide
  assign and_56_out = bit_extender_71_out & 4'b0100;  // AND_Gate and_56, 4 bits wide
  and and_57 (and_57_out, comparator_17_eq, 1'b0);
  and and_58 (and_58_out, comparator_18_eq, 1'b1);
  and and_59 (and_59_out, comparator_19_eq, 1'b0);
  and and_60 (and_60_out, comparator_20_eq, 1'b1);
  and and_61 (and_61_out, comparator_21_eq, 1'b0);
  and and_62 (and_62_out, comparator_22_eq, 1'b1);
  assign and_63_out = bit_extender_72_out & Imm8_Mov;  // AND_Gate and_63, 8 bits wide
  and and_64 (and_64_out, or_7_out, Shift_Codop);
  assign ALU_Opcode = and_54_out | and_55_out | and_56_out;  // OR_Gate or_9, 4 bits wide
  or or_10 (Carry, and_57_out, and_58_out, and_59_out, and_60_out, and_61_out, and_62_out);
  and and_65 (Imm32_Enable, or_8_out, Imm8_Codop);
  assign Imm32 = {{24{and_63_out[7]}}, and_63_out};  // Bit_Extender bit_extender_73
  assign bit_extender_74_out = {{4{and_64_out}}, and_64_out};  // Bit_Extender bit_extender_74
  assign Imm5 = bit_extender_74_out & imm5_Value;  // AND_Gate and_66, 5 bits wide

  assign Flags_Update_Mask[0] = 1'b0;

  // Other names for the same wires on the sheet: Carry_Out = Carry; Codeop[3:0] = ALU_Opcode;
  //   C_Flag_Value = Flags_Update_Mask[1]; Flag_Output[3:1] = Flags_Update_Mask[3:1];
  //   Z_Flag_Value = Flags_Update_Mask[2]; N_Flag_Value = Flags_Update_Mask[3]; Imm5_Output[4:0] = Imm5;
  //   Imm32_Out[31:0] = Imm32; output_for_RD[2:0] = Rd

  // Notes on the sheet:
  //   Note: ALU uses Rn register for shifts. Use Rn instead of Rm for shifts (immediate) here too
  //   Note 3: Imm32_Enable forces the use of the immediate for Rm register
  //   Note 2: MOV uses RSB ALU opcode with Imm8 reversed so that it is copied to output register
  //   Pull output low on Enable = 0
  //   only ADD and SUB use Rm
  //   Enable carry for SUB since it is reversed in ALU
  //   ALU will use Imm32 instead of Rm
endmodule
